# Fritzing sketch Untitled Sketch (saved by Fritzing 1.0.5)
breadboards: 1

parts:
  V1 = DC Power [voltage=12V]  # not connected
  HC-SR04_Sensor_1 = HC-SR04 Ultrasonic Distance Sensor
  Grove1 = Grove OLED 128x96
  DHT1 = DHT11 Humitidy and Temperature Sensor (3 pins)
  F1 = Fan - Ventilador [package=THT]
  U2 = Module 4 Relais 5V [package="Module 4 Relais 5V"]
  V2 = DC Power Supply
  S2 = Pushbutton [package="[SMD]"]
  LED1 = LED - 5mm [color="Red (633nm)" current=0.030A package="5 mm [THT]"]
  R1 = Resistor [tolerance=±5% power=0.25W resistance=220 package=THT]
  M1 = RioRand LM2596
  R2 = Resistor [tolerance=±5% power=0.25W resistance=10k package=THT]
  M2 = DC Motor [voltage_(max)=6V voltage_(min)=3V]  # not connected
  M3 = DC Motor [voltage_(max)=6V voltage_(min)=3V]  # not connected
  M4 = DC Motor [voltage_(max)=6V voltage_(min)=3V]  # not connected
  M5 = DC Motor [voltage_(max)=6V voltage_(min)=3V]  # not connected
  D1 = Rectifier Diode [part_number=1N4001 package="300 mil [THT]"]  # not connected
  D2 = Rectifier Diode [part_number=1N4001 package="300 mil [THT]"]  # not connected
  D3 = Rectifier Diode [part_number=1N4001 package="300 mil [THT]"]  # not connected
  D4 = Rectifier Diode [part_number=1N4001 package="300 mil [THT]"]  # not connected
  Part1 = Arduino Uno (Rev3)
  Q1 = Basic FET N-Channel [package="TO220 [THT]"]
  D5 = Rectifier Diode [part_number=1N4001 package="300 mil [THT]"]

nets:
  VCC: HC-SR04_Sensor_1.VCC, Grove1.VCC, DHT1.Plus, U2.VCC, S2.Pin_3, S2.Pin_4, R1.Pin_0, R2.Pin_1, Part1.5V
  N1: HC-SR04_Sensor_1.TRIG, Part1.D8
  N2: HC-SR04_Sensor_1.ECHO, Part1.D9_PWM
  GND: HC-SR04_Sensor_1.GND, Grove1.GND, DHT1.Gnd, U2.GND, Part1.GND
  N3: Grove1.SDA, Part1.A4/SDA
  N4: Grove1.SCL, Part1.A5/SCL
  N5: DHT1.Signal, Part1.D10_PWM/SS
  N6: F1.5V, M1.Pin_3, D5.cathode
  N7: F1.GND, Q1.drain, D5.anode
  N8: U2.IN1, Part1.D2
  N9: U2.IN2, Part1.D3_PWM
  N10: U2.IN3, Part1.D4
  N11: U2.IN4, Part1.D5_PWM
  N12: V2.Pin_2, M1.Pin_1
  N13: V2.Pin_1, M1.Pin_2
  N14: S2.Pin_1, S2.Pin_2, R2.Pin_0, Part1.D11_PWM/MOSI
  N15: LED1.cathode, R1.Pin_1
  N16: LED1.anode, Part1.D12/MISO
  N17: M1.Pin_4, Q1.source
  N18: Part1.D7, Q1.gate

notes:
  500mA
  15mA
  0.3mA
  20mA
  1.4A
  3A max

custom parts:
  DHT11 Humitidy and Temperature Sensor (3 pins): DHT11 Humidity and Temperature Sensor (3 pins).
  Fan - Ventilador: Ventilador de 2 pines, se encuentra comunmente en computadoras de escritorio
  Module 4 Relais 5V: Module 4 Relais 5V 4x SPD-06VDC-SD-C
  DC Power Supply: DC Power Supply 30V5A.
